# Fritzing sketch ConexionBluetoothMega (saved by Fritzing 0.9.3b)
breadboards: 1

parts:
  Componente1 = Bluetooth HC-05 Macho
  Componente2 = Arduino Mega 2560 (Rev3)
  Componente3 = Arduino Mega 2560 (Rev3)
  Componente4 = Bluetooth HC-05 Macho
  R1 = Resistor [tolerance=±5% resistance=330 package=THT]
  R2 = Resistor [tolerance=±5% resistance=330 package=THT]
  R3 = Resistor [tolerance=±5% resistance=330 package=THT]
  LED1 = LED - 5mm [color="Red (633nm)" package="5 mm [THT]"]
  LED2 = LED - 5mm [color="Red (633nm)" package="5 mm [THT]"]
  LED3 = LED - 5mm [color="Red (633nm)" package="5 mm [THT]"]

nets:
  N1: Componente1.TXD, Componente2.D0_RX0
  N2: Componente1.RXD, Componente2.D1_TX0
  VCC: Componente1.VCC, Componente2.5V
  GND: Componente1.GND, Componente2.GND
  GND_2: Componente3.GND, Componente4.GND, R1.Pin_0, R2.Pin_0, R3.Pin_0
  N3: Componente3.D13_PWM, LED3.anode
  N4: Componente3.D12_PWM, LED2.anode
  N5: Componente3.D11_PWM, LED1.anode
  N6: Componente3.D0_RX0, Componente4.TXD
  N7: Componente3.D1_TX0, Componente4.RXD
  5V: Componente3.5V, Componente4.VCC
  N8: R1.Pin_1, LED1.cathode
  N9: R2.Pin_1, LED2.cathode
  N10: R3.Pin_1, LED3.cathode
