# Fritzing sketch ControladorRGB (saved by Fritzing 0.9.3b)
breadboards: 1

parts:
  Componente1 = Bluetooth HC-05 Macho
  Componente2 = Arduino Mega 2560 (Rev3)
  Componente3 = Arduino Mega 2560 (Rev3)
  Componente4 = Bluetooth HC-05 Macho
  R1 = Resistor [tolerance=±5% resistance=1k package=THT]
  R2 = Resistor [tolerance=±5% resistance=1k package=THT]
  R3 = Resistor [tolerance=±5% resistance=1k package=THT]
  Q1 = pnp-Powertransistor [package="TO220 [THT]"]  # not connected
  Q2 = pnp-Powertransistor [package="TO220 [THT]"]
  Q3 = pnp-Powertransistor [package="TO220 [THT]"]
  VCC1 = Battery
  LED1 = Super Flux RGB LED (com. cathode)

nets:
  N1: Componente1.TXD, Componente2.D0_RX0
  N2: Componente1.RXD, Componente2.D1_TX0
  VCC: Componente1.VCC, Componente2.5V
  GND: Componente1.GND, Componente2.GND, Q2.collector, Q3.collector, VCC1.-
  N3: Componente2.VIN, LED1.common_cathode
  N4: Componente2.D2_PWM, R1.Pin_1
  N5: Componente2.D3_PWM, R3.Pin_1
  N6: Componente2.D4_PWM, R2.Pin_1
  N7: Componente3.D19/RX1, Componente4.TXD
  N8: Componente3.D18/TX1, Componente4.RXD
  5V: Componente3.5V, Componente4.VCC
  GND_2: Componente3.GND, Componente4.GND
  N9: R2.Pin_0, Q3.base
  N10: R3.Pin_0, Q2.base
  N11: Q2.emitter, LED1.green_anode
  N12: Q3.emitter, LED1.blue_anode

notes:
  Este arduino va conectado a la computadora
  12V 6A power supply
  Tip31
